# Fritzing sketch ESP32_TFT_Module (saved by Fritzing 0.9.5d)

parts:
  LCD2 = TFT 1.8 inch 160x128 w SD
  esp1 = ESP32 DevKitc V4

nets:
  N1: LCD2.pin_1, esp1.5V
  N2: LCD2.pin2, esp1.GND
  N3: LCD2.pin_9, esp1.IO15
  N4: LCD2.pin_10, esp1.IO23
  N5: LCD2.pin_11, esp1.IO19
  N6: LCD2.pin_12, esp1.IO18

custom parts:
  TFT 1.8 inch 160x128 w SD: This is a generic 1.8 tft spi lcd display available on ebay and others. The 1.8" display has 128x160 color pixels.
  ESP32 DevKitc V4: ESP32-DevKitC board with ESP32-WROOM-32 module. ESP32-DevKitC V4 is a small-sized ESP32-based development board produced by Espressif. Most of the pins on the ESP module are broken out to the pin headers on the board. The pins D0, D1, D2, D3, CMD and CLK are used internally for communication between ESP32 and SPI flash memory. They are grouped on both sides near the USB connector. Avoid using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
