# Fritzing sketch MainModule (saved by Fritzing 0.9.5d)

parts:
  esp1 = ESP32 DevKitc V4
  RY1 = SSR-40VA
  M1 = ph-4502c [package=THT]
  M2 = water level switch
  DS1 = DS18B20 1-Wire Temperature Sensor Probe
  Q1 = Basic FET N-Channel [package="DPak [SMD]"]
  J1 = Camdenboss CTB0158-2 [part_number=CTB0158-2 package=THT]
  J2 = Camdenboss CTB0158-2 [part_number=CTB0158-2 package=THT]
  M3 = PH meter with sensor in breadboard [package=THT]
  R1 = Resistor [tolerance=±5% resistance=10k package="2010 [SMD]"]

nets:
  N1: esp1.IO2, DS1.DQ
  GND: esp1.GND, esp1.IO32, M1.pin4, M1.pin5, DS1.GND, M3.pin3
  N2: esp1.IO34, Q1.Gate
  N3: esp1.IO35, M2.pin2
  N4: esp1.IO33, M3.pin1
  N5: esp1.IO25, RY1.Pin_3
  N6: esp1.CMD, RY1.Pin_4, M2.pin1, R1.Pin_0
  5V: esp1.5V, M1.pin6, DS1.VDD, J2.terminal_2, M3.pin2
  N7: RY1.Pin_2, J1.terminal_2
  N8: Q1.drain, J2.terminal_1

custom parts:
  ESP32 DevKitc V4: ESP32-DevKitC board with ESP32-WROOM-32 module. ESP32-DevKitC V4 is a small-sized ESP32-based development board produced by Espressif. Most of the pins on the ESP module are broken out to the pin headers on the board. The pins D0, D1, D2, D3, CMD and CLK are used internally for communication between ESP32 and SPI flash memory. They are grouped on both sides near the USB connector. Avoid using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
  SSR-40VA: SSR-40VA solid state relay.
  ph-4502c: ph-4502c PH Meter.
  water level switch: Generic water level float switch.
  PH meter with sensor in breadboard: DFrobot PH meter (SKU SEN0161)
